# Fritzing sketch DomoHome_battery_control (saved by Fritzing 0.9.3b)

parts:
  WeMos_D1_Mini2 = WeMos D1 Mini
  Rtop = Resistor [tolerance=±5% resistance=47k package=THT]
  Rbottom = Resistor [tolerance=±5% resistance=10k package=THT]
  12V_Baterry = Lilypad Battery Connect

nets:
  N1: WeMos_D1_Mini2.A0, Rtop.Pin_0, Rbottom.Pin_1
  N2: WeMos_D1_Mini2.G, Rbottom.Pin_0, 12V_Baterry.-
  N3: Rtop.Pin_1, 12V_Baterry.+
